# Fritzing sketch Home-Automation-PCB (saved by Fritzing 0.9.2b)
circuit board: 9.22482cm x 7.41024cm
breadboards: 1

parts:
  TX433N = female pin header, 4 pins [form="♀ (female)"]
  Serial_Port = female pin header, 6 pins [form="♀ (female)"]
  Antenna = female pin header, 1 pin [form="♀ (female)"]
  ULN2803A = ULN2803 Darlington Array
  IR_Receiver = female pin header, 3 pins [form="♀ (female)"]
  Speaker_1_Input = female pin header, 2 pins [form="♀ (female)"]
  Speaker_2 = female pin header, 2 pins [form="♀ (female)"]
  Spk_2_In = female pin header, 2 pins [form="♀ (female)"]
  Spk_2_Out = female pin header, 2 pins [form="♀ (female)"]
  R2_-_8_2 = Resistor [tolerance=±5% resistance=8.2 package=THT]
  IR_LED_3 = female pin header, 2 pins [form="♀ (female)"]
  IR_LED_2 = female pin header, 2 pins [form="♀ (female)"]
  IR_LED_1 = female pin header, 2 pins [form="♀ (female)"]
  BUTTON_1 = female pin header, 2 pins [form="♀ (female)"]
  R3_-_1k = Resistor [tolerance=±5% resistance=1k package=THT]
  R4_-_10k = Resistor [tolerance=±5% resistance=10k package=THT]
  BUTTON_2 = female pin header, 2 pins [form="♀ (female)"]
  R3_-_1k_2 = Resistor [tolerance=±5% resistance=1k package=THT]
  BUTTON_3 = female pin header, 2 pins [form="♀ (female)"]
  R3_-_1k_3 = Resistor [tolerance=±5% resistance=1k package=THT]
  BUTTON_4 = female pin header, 2 pins [form="♀ (female)"]
  R3_-_1k_4 = Resistor [tolerance=±5% resistance=1k package=THT]
  G5V-1-DC5 = RELAY-2 [package=relay-g5v]
  G5V-1-DC5_2 = RELAY-2 [package=relay-g5v]
  TV_ELEVATOR = female pin header, 3 pins [form="♀ (female)"]
  R4_-_10k_2 = Resistor [tolerance=±5% resistance=10k package=THT]
  R4_-_10k_3 = Resistor [tolerance=±5% resistance=10k package=THT]
  R4_-_10k_4 = Resistor [tolerance=±5% resistance=10k package=THT]
  R5_-_1_2k = Resistor [tolerance=±5% resistance=1.2k package=THT]
  R5_-_? = Resistor [tolerance=±5% resistance=1.2k package=THT]
  R5_-_?_2 = Resistor [tolerance=±5% resistance=1.2k package=THT]
  R5_-_?_3 = Resistor [tolerance=±5% resistance=1.2k package=THT]
  R5_-_?_4 = Resistor [tolerance=±5% resistance=1.2k package=THT]
  D1 = Rectifier Diode [part_number=1N4001 package="300 mil [THT]"]
  D2 = Rectifier Diode [part_number=1N4001 package="300 mil [THT]"]
  D3 = Rectifier Diode [part_number=1N4001 package="300 mil [THT]"]
  D4 = Rectifier Diode [part_number=1N4001 package="300 mil [THT]"]
  Raspberry_Pi = Cobbler Plus
  Speaker_1_Input1 = female pin header, 2 pins [form="♀ (female)"]
  Speaker_1_Input2 = female pin header, 2 pins [form="♀ (female)"]
  Speaker_1_Input3 = female pin header, 2 pins [form="♀ (female)"]
  Speaker_1_Input4 = female pin header, 2 pins [form="♀ (female)"]
  VR05R051A = DIP-Relay-VR05R051'A [part_number=VR05R051'A]
  VR05R051A_2 = DIP-Relay-VR05R051'A [part_number=VR05R051'A]
  Temp_Humidity_2 = rounded female pin header, 4 pins [form="♀ (female rounded)"]
  Temp_Humidity_1 = rounded female pin header, 4 pins [form="♀ (female rounded)"]
  R1_-_4_7k = Resistor [tolerance=±5% resistance=4.7k package=THT]
  R1_-_4_7k_2 = Resistor [tolerance=±5% resistance=4.7k package=THT]
  SMI-05VDC-SL-2C = Relay - SMI-05VDC-SL-2C [part_number=relay-SMI-05VDC-SL-2C]

nets:
  N1: TX433N.pin1, Raspberry_Pi.GND#8
  N2: TX433N.pin2, Raspberry_Pi.#17
  N3: TX433N.pin3, R2_-_8_2.Pin_0, G5V-1-DC5.2, G5V-1-DC5_2.2, D1.cathode, D2.cathode, D3.cathode, D4.cathode, Raspberry_Pi.5.0V#1, VR05R051A.Coil2_-, VR05R051A_2.Coil2_-, SMI-05VDC-SL-2C.COIL_2+
  N4: TX433N.pin4, Antenna.pin1
  N5: Serial_Port.pin3, IR_Receiver.pin2, Raspberry_Pi.GND#13, Temp_Humidity_2.pin4, Temp_Humidity_1.pin4
  N6: Serial_Port.pin4, Raspberry_Pi.RXD
  N7: Serial_Port.pin5, Raspberry_Pi.TXD
  N8: Serial_Port.pin6, Raspberry_Pi.3V3, Temp_Humidity_2.pin1, Temp_Humidity_1.pin1, R1_-_4_7k.Pin_0, R1_-_4_7k_2.Pin_1
  N9: ULN2803A.I4, R5_-_1_2k.Pin_1
  N10: ULN2803A.I5, R5_-_?.Pin_1
  N11: ULN2803A.I6, R5_-_?_2.Pin_1
  N12: ULN2803A.I7, R5_-_?_3.Pin_1
  N13: ULN2803A.I8, R5_-_?_4.Pin_1
  N14: ULN2803A.GND, Raspberry_Pi.GND#24
  N15: ULN2803A.O8, VR05R051A_2.COIL1_+#12
  N16: ULN2803A.O7, D4.anode, SMI-05VDC-SL-2C.COIL_1-
  N17: ULN2803A.O6, G5V-1-DC5_2.9, D1.anode
  N18: ULN2803A.O5, G5V-1-DC5.9, D2.anode
  N19: ULN2803A.O4, IR_LED_3.pin1, IR_LED_2.pin1, IR_LED_1.pin1
  N20: IR_Receiver.pin1, Raspberry_Pi.#23
  N21: IR_Receiver.pin3, Raspberry_Pi.5.0V#3
  N22: Speaker_1_Input.pin1, Speaker_1_Input3.pin1
  N23: Speaker_1_Input.pin2, SMI-05VDC-SL-2C.NC_2
  N24: Speaker_2.pin1, Speaker_1_Input1.pin1
  N25: Speaker_2.pin2, SMI-05VDC-SL-2C.NC_1
  N26: Spk_2_In.pin1, Speaker_1_Input2.pin1
  N27: Spk_2_In.pin2, VR05R051A_2.A2_Switch_Terminal_A
  N28: Spk_2_Out.pin1, Speaker_1_Input4.pin1
  N29: Spk_2_Out.pin2, VR05R051A.A2_Switch_Terminal_A
  N30: R2_-_8_2.Pin_1, IR_LED_3.pin2, IR_LED_2.pin2, IR_LED_1.pin2
  N31: BUTTON_1.pin1, BUTTON_2.pin1, BUTTON_3.pin1, BUTTON_4.pin1, Raspberry_Pi.3.3V
  N32: BUTTON_1.pin2, R3_-_1k.Pin_0, R4_-_10k.Pin_0
  N33: R3_-_1k.Pin_1, Raspberry_Pi.#12
  N34: R4_-_10k.Pin_1, R4_-_10k_2.Pin_1, R4_-_10k_3.Pin_1, R4_-_10k_4.Pin_1, Raspberry_Pi.GND#33
  N35: BUTTON_2.pin2, R3_-_1k_2.Pin_0, R4_-_10k_2.Pin_0
  N36: R3_-_1k_2.Pin_1, Raspberry_Pi.#16
  N37: BUTTON_3.pin2, R3_-_1k_3.Pin_0, R4_-_10k_3.Pin_0
  N38: R3_-_1k_3.Pin_1, Raspberry_Pi.#20
  N39: BUTTON_4.pin2, R3_-_1k_4.Pin_0, R4_-_10k_4.Pin_0
  N40: R3_-_1k_4.Pin_1, Raspberry_Pi.#21
  N41: G5V-1-DC5.5, G5V-1-DC5_2.1
  N42: G5V-1-DC5.10, TV_ELEVATOR.pin3
  N43: G5V-1-DC5_2.6, TV_ELEVATOR.pin1
  N44: G5V-1-DC5_2.10, TV_ELEVATOR.pin2
  N45: R5_-_1_2k.Pin_0, Raspberry_Pi.#26
  N46: R5_-_?.Pin_0, Raspberry_Pi.#19
  N47: R5_-_?_2.Pin_0, Raspberry_Pi.#13
  N48: R5_-_?_3.Pin_0, Raspberry_Pi.#6
  N49: R5_-_?_4.Pin_0, Raspberry_Pi.#5
  N50: D3.anode, VR05R051A.COIL1_+, VR05R051A_2.COIL1_+#1
  N51: Raspberry_Pi.#24, Temp_Humidity_2.pin2, R1_-_4_7k_2.Pin_0
  N52: Raspberry_Pi.#25, Temp_Humidity_1.pin2, R1_-_4_7k.Pin_1
  N53: Speaker_1_Input1.pin2, SMI-05VDC-SL-2C.MAIN_1
  N54: Speaker_1_Input2.pin2, VR05R051A_2.B1_Switch_Terminal_B
  N55: Speaker_1_Input3.pin2, SMI-05VDC-SL-2C.MAIN_2
  N56: Speaker_1_Input4.pin2, VR05R051A.B1_Switch_Terminal_B

notes:
  ANTENNA
  VCC
  DATA
  GND
  RXD
  COM
  UP
  DOWN
  Right
  Home Automation System
  Left Out
  Spk. 1
  Left In
  Left In   Left Out
  Red White   Red White
  Speaker Pair 1
  Left In    Left Out
  Right In   Right Out
  Speaker Pair 2
  TXD
  VDD
  NULL
  Designed by Henrik and Robert Nilsson
  https://github.com/SoShibby/Home-Automation-PCB
  Rev 1.0

custom parts:
  ULN2803 Darlington Array: ULN2803 Darlington Transistor Array with Flyback Protection
  Cobbler Plus: The Cobbler Plus is an add on prototyping board from Adafruit specifically designed for the Raspberry Pi B+ that can break out all those tasty power, GPIO, I2C and SPI pins from the 40-pin header onto a solderless breadboard. This set will make "cobbling together" prototypes with the Pi super easy. The Cobbler Plus can plug into any solderless breadboard.
  DIP-Relay-VR05R051'A: Dip-Relay
  Relay - SMI-05VDC-SL-2C: DPDT relay
